// Logisim project IT012_Lab01_25520311.circ as structural Verilog: 6 circuits, main circuit Warmup
module Warmup (
  input  A,
  input  B,
  output F
);

  wire not_1_out;

  not not_1 (not_1_out, B);
  and and_1 (F, A, not_1_out);
endmodule

module TN1 (
  input  A,
  input  B,
  input  C,
  output NOT,
  output AND,
  output OR,
  output NAND,
  output NOR,
  output XOR,
  output XNOR,
  output XOR3,
  output NAND3,
  output CHAIN
);

  not not_1 (NOT, A);
  and and_1 (AND, A, B);
  or or_1 (OR, A, B);
  nand nand_1 (NAND, A, B);
  nor nor_1 (NOR, A, B);
  xor xor_1 (XOR, A, B);
  xnor xnor_1 (XNOR, A, B);
  xor xor_2 (XOR3, A, B, C);
  nand nand_2 (NAND3, A, B, C);
  nand nand_3 (CHAIN, NAND, C);
endmodule

module TN2 (
  input  X,
  input  Y,
  input  Z,
  output EQ1,
  output EQ2,
  output EQ3,
  output EQ4,
  output EQ5
);

  wire not_1_out, not_2_out, not_3_out, x___x_prime_y_out, x___y___x___z_out, x___y_prime_out, x___y_z_out,
       x___z_out, x_prime_y_out, x_prime_y_prime_out, x_y__prime_out, x_y_out, y_z_out;

  not not_1 (not_1_out, X);
  not not_2 (not_2_out, Y);
  and x_y__prime (x_y__prime_out, X, Y);
  and y_z (y_z_out, Y, Z);
  and x_prime_y (x_prime_y_out, Y, not_1_out);
  nor x___y_prime (x___y_prime_out, X, Y);
  and x_prime_y_prime (x_prime_y_prime_out, not_1_out, not_2_out);
  not not_3 (not_3_out, x_y__prime_out);
  or x___y_z (x___y_z_out, X, y_z_out);
  or x_y (x_y_out, X, Y);
  or x___z (x___z_out, X, Z);
  or x___x_prime_y (x___x_prime_y_out, x_prime_y_out, X);
  xnor xnor_1 (EQ1, x___y_prime_out, x_prime_y_prime_out);
  xnor xnor_2 (EQ2, x_prime_y_prime_out, not_3_out);
  and x___y___x___z (x___y___x___z_out, x_y_out, x___z_out);
  xnor xnor_3 (EQ4, x___x_prime_y_out, X);
  xnor xnor_4 (EQ5, x_y_out, x___x_prime_y_out);
  xnor xnor_5 (EQ3, x___y_z_out, x___y___x___z_out);
endmodule

module TN3 (
  input  A,
  input  B,
  input  C,
  input  D,
  output F
);

  wire _2_out, _3_out, _5_out, _7_out, _11_out, _13_out, not_1_out, not_2_out, not_3_out, not_4_out;

  not not_1 (not_1_out, A);
  not not_2 (not_2_out, B);
  not not_3 (not_3_out, C);
  not not_4 (not_4_out, D);
  and _2 (_2_out, not_1_out, not_2_out, C, not_4_out);
  and _3 (_3_out, not_1_out, not_2_out, C, D);
  and _5 (_5_out, not_1_out, B, not_3_out, D);
  and _7 (_7_out, not_1_out, B, C, D);
  and _11 (_11_out, A, not_2_out, C, D);
  and _13 (_13_out, A, B, not_3_out, D);
  or N (F, _2_out, _3_out, _5_out, _7_out, _11_out, _13_out);
endmodule

module TN4 (
  input  A,
  input  B,
  input  C,
  input  D,
  output F_can,
  output EQ1,
  output EQ2
);

  wire _2_out, _3_out, _5_out, _7_out, _11_out, _13_out, A_prime___B_prime___C_prime_out, A_prime___D_out,
       A_prime_B_prime_C_out, A_prime_BD_out, B___C_out, B_prime___D_out, B_prime_CD_out, BC_prime_D_out,
       F_pos_out, not_1_out, not_2_out, not_3_out, not_4_out;

  not not_1 (not_1_out, A);
  not not_2 (not_2_out, B);
  not not_3 (not_3_out, C);
  not not_4 (not_4_out, D);
  and _2 (_2_out, not_1_out, not_2_out, C, not_4_out);
  and _3 (_3_out, not_1_out, not_2_out, C, D);
  and _5 (_5_out, not_1_out, B, not_3_out, D);
  and _7 (_7_out, not_1_out, B, C, D);
  and _11 (_11_out, A, not_2_out, C, D);
  and _13 (_13_out, A, B, not_3_out, D);
  and A_prime_B_prime_C (A_prime_B_prime_C_out, not_1_out, not_2_out, C);
  and B_prime_CD (B_prime_CD_out, not_2_out, C, D);
  and A_prime_BD (A_prime_BD_out, not_1_out, B, D);
  and BC_prime_D (BC_prime_D_out, B, not_3_out, D);
  or A_prime___D (A_prime___D_out, not_1_out, D);
  or B___C (B___C_out, B, C);
  or B_prime___D (B_prime___D_out, not_2_out, D);
  or A_prime___B_prime___C_prime (A_prime___B_prime___C_prime_out, not_1_out, not_2_out, not_3_out);
  or N (F_can, _2_out, _3_out, _5_out, _7_out, _11_out, _13_out);
  or F_sop (F_can, A_prime_B_prime_C_out, B_prime_CD_out, A_prime_BD_out, BC_prime_D_out);
  and F_pos (F_pos_out, A_prime___D_out, B___C_out, B_prime___D_out, A_prime___B_prime___C_prime_out);
  xnor xnor_1 (EQ1, F_can, F_can);
  xnor xnor_2 (EQ2, F_can, F_pos_out);
endmodule

module TN5 (
  input  A,
  input  B,
  input  C,
  output F
);

  wire xor_1_out;

  xor xor_1 (xor_1_out, A, B);
  xor xor_2 (F, xor_1_out, C);
endmodule
