// Logisim project IT012_Lab02_25520311.circ as structural Verilog: 8 circuits, main circuit FA
module FA (
  input  A,
  input  B,
  input  Cin,
  output S,
  output Cout
);

  wire and_1_out, and_2_out, xor_1_out;

  xor xor_1 (xor_1_out, A, B);
  and and_1 (and_1_out, A, B);
  xor xor_2 (S, xor_1_out, Cin);
  and and_2 (and_2_out, Cin, xor_1_out);
  or or_1 (Cout, and_1_out, and_2_out);
endmodule

module ADDSUB4 (
  input  [3:0] A,
  input  [3:0] B,
  input  SUB,
  output [3:0] S,
  output C
);

  wire fa_1_cout, fa_2_cout, fa_3_cout, xor_1_out, xor_2_out, xor_3_out, xor_4_out;

  // Probe on fa_1_cout
  FA fa_1 (.A(A[0]), .B(xor_1_out), .Cin(SUB), .S(S[0]), .Cout(fa_1_cout));
  xor xor_1 (xor_1_out, B[0], SUB);
  FA fa_2 (.A(A[1]), .B(xor_2_out), .Cin(fa_1_cout), .S(S[1]), .Cout(fa_2_cout));
  xor xor_2 (xor_2_out, B[1], SUB);
  // Probe on fa_2_cout
  FA fa_3 (.A(A[2]), .B(xor_3_out), .Cin(fa_2_cout), .S(S[2]), .Cout(fa_3_cout));
  xor xor_3 (xor_3_out, B[2], SUB);
  // Probe on fa_3_cout
  FA fa_4 (.A(A[3]), .B(xor_4_out), .Cin(fa_3_cout), .S(S[3]), .Cout(C));
  xor xor_4 (xor_4_out, B[3], SUB);
endmodule

module ALU8 (
  input  [7:0] A,
  input  [7:0] B,
  input  [2:0] OP,
  output LT,
  output Z,
  output [7:0] R
);

  wire [7:0] adder_1_out, adder_2_out, and_1_out, multiplexer_1_out, multiplexer_2_out, not_1_out, or_1_out,
       subtractor_1_out, subtractor_2_out, xor_1_out;

  Adder adder_1 (.a(A), .b(B), .out(adder_1_out));  // open: cin, cout
  Adder adder_2 (.a(A), .b(8'h1), .out(adder_2_out));  // open: cin, cout
  Subtractor subtractor_1 (.a(A), .b(B), .out(subtractor_1_out));  // open: bin, bout
  Subtractor subtractor_2 (.a(A), .b(8'h1), .out(subtractor_2_out));  // open: bin, bout
  assign and_1_out = A & B;  // AND_Gate and_1, 8 bits wide
  assign or_1_out = A | B;  // OR_Gate or_1, 8 bits wide
  assign not_1_out = ~A;  // NOT_Gate not_1, 8 bits wide
  assign xor_1_out = A ^ B;  // XOR_Gate xor_1, 8 bits wide
  Multiplexer #(.select(2), .width(8)) multiplexer_1 (
    .in0(adder_1_out), .in1(adder_2_out), .in2(subtractor_1_out), .in3(subtractor_2_out),
    .out(multiplexer_1_out), .sel(OP[1:0]));  // open: en
  Multiplexer #(.select(2), .width(8)) multiplexer_2 (
    .in0(and_1_out), .in1(or_1_out), .in2(not_1_out), .in3(xor_1_out), .out(multiplexer_2_out), .sel(OP[1:0]));  // open: en
  LT lt_1 (.A7(A[7]), .B7(B[7]), .R7(R[7]), .LT(LT));
  Multiplexer #(.width(8)) multiplexer_3 (
    .in0(multiplexer_1_out), .in1(multiplexer_2_out), .out(R), .sel(OP[2]));  // open: en
  nor nor_1 (Z, R[0], R[1], R[2], R[3], R[4], R[5], R[6], R[7]);
endmodule

module LT (
  input  A7,
  input  B7,
  input  R7,
  output LT
);

  wire A7B7_prime_out, A7R7_out, B7_prime_R7_out, not_1_out;

  not not_1 (not_1_out, B7);
  and A7R7 (A7R7_out, A7, R7);
  and B7_prime_R7 (B7_prime_R7_out, not_1_out, R7);
  and A7B7_prime (A7B7_prime_out, A7, not_1_out);
  or or_1 (LT, A7B7_prime_out, A7R7_out, B7_prime_R7_out);
endmodule

module DLATCH (
  input  D,
  input  E,
  output Q
);

  Multiplexer multiplexer_1 (.in0(Q), .in1(D), .out(Q), .sel(E));  // open: en
endmodule

module TN3 (
  input  D,
  input  CLK,
  output _2_DLATCH,
  output _2_D_Flip_Flop,
  output Q1,
  output Q2
);

  wire d_ff_1_q, dlatch_1_q;

  DLATCH dlatch_1 (.D(D), .E(CLK), .Q(dlatch_1_q));
  DLATCH dlatch_2 (.D(dlatch_1_q), .E(CLK), .Q(_2_DLATCH));
  D_Flip_Flop d_ff_1 (.clk(CLK), .D(D), .Q(d_ff_1_q));  // open: Qn, preset, en, reset
  DLATCH dlatch_3 (.D(D), .E(CLK), .Q(Q1));
  D_Flip_Flop d_ff_2 (.clk(CLK), .D(D), .Q(Q2));  // open: Qn, preset, en, reset
  D_Flip_Flop d_ff_3 (.clk(CLK), .D(d_ff_1_q), .Q(_2_D_Flip_Flop));  // open: Qn, preset, en, reset
endmodule

module REGFILE (
  input  [7:0] \DỊN ,
  input  WE,
  input  [1:0] RD,
  input  CLK,
  input  [1:0] RA,
  input  [1:0] RB,
  output [7:0] R0,
  output [7:0] QA,
  output [7:0] R1,
  output [7:0] R2,
  output [7:0] QB,
  output [7:0] R3
);

  wire decoder_1_out0, decoder_1_out1, decoder_1_out2, decoder_1_out3;

  Decoder #(.select(2), .disabled(0)) decoder_1 (
    .out0(decoder_1_out0), .out1(decoder_1_out1), .out2(decoder_1_out2), .out3(decoder_1_out3), .sel(RD),
    .en(WE));
  Register register_1 (.D(\DỊN ), .en(decoder_1_out0), .Q(R0), .clk(CLK));  // open: clr
  Register register_2 (.D(\DỊN ), .en(decoder_1_out1), .Q(R1), .clk(CLK));  // open: clr
  Register register_3 (.D(\DỊN ), .en(decoder_1_out2), .Q(R2), .clk(CLK));  // open: clr
  Register register_4 (.D(\DỊN ), .en(decoder_1_out3), .Q(R3), .clk(CLK));  // open: clr
  Multiplexer #(.select(2), .width(8)) multiplexer_1 (
    .in0(R0), .in1(R1), .in2(R2), .in3(R3), .out(QA), .sel(RA));  // open: en
  Multiplexer #(.select(2), .width(8)) multiplexer_2 (
    .in0(R0), .in1(R1), .in2(R2), .in3(R3), .out(QB), .sel(RB));  // open: en
endmodule

module DATAPATH (
  input  WE,
  input  SRC,
  input  [1:0] RD,
  input  CLK,
  input  [1:0] RA,
  input  [7:0] IMM,
  input  [1:0] RB,
  input  [2:0] OP,
  output [7:0] R0,
  output [7:0] R1,
  output Z,
  output [7:0] R,
  output [7:0] R2,
  output [7:0] R3
);

  wire [7:0] multiplexer_1_out, regfile_1_qa, regfile_1_qb;

  REGFILE regfile_1 (
    .\DỊN (multiplexer_1_out), .WE(WE), .RD(RD), .CLK(CLK), .RA(RA), .RB(RB), .R0(R0), .QA(regfile_1_qa),
    .R1(R1), .R2(R2), .QB(regfile_1_qb), .R3(R3));
  ALU8 alu8_1 (.A(regfile_1_qa), .B(regfile_1_qb), .OP(OP), .Z(Z), .R(R));  // open: LT
  Multiplexer #(.width(8)) multiplexer_1 (.in0(R), .in1(IMM), .out(multiplexer_1_out), .sel(SRC));  // open: en
endmodule
