// Logisim project TN1.circ as structural Verilog
module Warmup (
  input  A,
  input  B,
  input  C,
  output NOT,
  output AND,
  output OR,
  output NAND,
  output NOR,
  output XOR,
  output XNOR,
  output XOR3,
  output NAND3,
  output CHAIN
);

  not not_1 (NOT, A);
  and and_1 (AND, A, B);
  or or_1 (OR, A, B);
  nand nand_1 (NAND, A, B);
  nor nor_1 (NOR, A, B);
  xor xor_1 (XOR, A, B);
  xnor xnor_1 (XNOR, A, B);
  xor xor_2 (XOR3, A, B, C);
  nand nand_2 (NAND3, A, B, C);
  nand nand_3 (CHAIN, NAND, C);
endmodule
