// Logisim project TN2.circ as structural Verilog
module TN2 (
  input  X,
  input  Y,
  input  Z,
  output EQ1,
  output EQ2,
  output EQ3,
  output EQ4,
  output EQ5
);

  wire not_1_out, not_2_out, not_3_out, x___x_prime_y_out, x___y___x___z_out, x___y_prime_out, x___y_z_out,
       x___z_out, x_prime_y_out, x_prime_y_prime_out, x_y__prime_out, x_y_out, y_z_out;

  not not_1 (not_1_out, X);
  not not_2 (not_2_out, Y);
  and x_y__prime (x_y__prime_out, X, Y);
  and y_z (y_z_out, Y, Z);
  and x_prime_y (x_prime_y_out, Y, not_1_out);
  nor x___y_prime (x___y_prime_out, X, Y);
  and x_prime_y_prime (x_prime_y_prime_out, not_1_out, not_2_out);
  not not_3 (not_3_out, x_y__prime_out);
  or x___y_z (x___y_z_out, X, y_z_out);
  or x_y (x_y_out, X, Y);
  or x___z (x___z_out, X, Z);
  or x___x_prime_y (x___x_prime_y_out, x_prime_y_out, X);
  xnor xnor_1 (EQ1, x___y_prime_out, x_prime_y_prime_out);
  xnor xnor_2 (EQ2, x_prime_y_prime_out, not_3_out);
  and x___y___x___z (x___y___x___z_out, x_y_out, x___z_out);
  xnor xnor_3 (EQ4, x___x_prime_y_out, X);
  xnor xnor_4 (EQ5, x_y_out, x___x_prime_y_out);
  xnor xnor_5 (EQ3, x___y_z_out, x___y___x___z_out);
endmodule
