// Logisim project TN3.circ as structural Verilog: 1 circuit, main circuit main
module main (
  input  A,
  input  B,
  input  C,
  input  D,
  output F
);

  wire _2_out, _3_out, _5_out, _7_out, _11_out, _13_out, not_1_out, not_2_out, not_3_out, not_4_out;

  not not_1 (not_1_out, A);
  not not_2 (not_2_out, B);
  not not_3 (not_3_out, C);
  not not_4 (not_4_out, D);
  and _2 (_2_out, not_1_out, not_2_out, C, not_4_out);
  and _3 (_3_out, not_1_out, not_2_out, C, D);
  and _5 (_5_out, not_1_out, B, not_3_out, D);
  and _7 (_7_out, not_1_out, B, C, D);
  and _11 (_11_out, A, not_2_out, C, D);
  and _13 (_13_out, A, B, not_3_out, D);
  or N (F, _2_out, _3_out, _5_out, _7_out, _11_out, _13_out);
endmodule
